// Logisim project 计算机组件仿真.circ as structural Verilog
module \全加器  (
  input  in_1,
  input  in_2,
  input  in_3,
  output out_4,
  output out_5
);

  wire \半加器_1_out_3 , \半加器_1_out_4 , \半加器_2_out_4 ;

  \半加器  \u_半加器_1  (.in_1(in_2), .in_2(in_3), .out_3(\半加器_1_out_3 ), .out_4(\半加器_1_out_4 ));
  \半加器  \u_半加器_2  (.in_1(in_1), .in_2(\半加器_1_out_3 ), .out_3(out_4), .out_4(\半加器_2_out_4 ));
  or or_1 (out_5, \半加器_2_out_4 , \半加器_1_out_4 );
endmodule

module \改进加法器  (
  input  in_1,
  input  in_2,
  input  in_3,
  input  in_4,
  input  in_5,
  input  in_6,
  input  in_7,
  input  in_8,
  input  in_9,
  input  in_10,
  input  in_11,
  input  in_12,
  input  in_13,
  input  in_14,
  input  in_15,
  input  in_16,
  input  in_17,
  input  in_18,
  input  in_19
);

  wire \n8位加法器_1_out_18 , \n8位加法器_1_out_19 , \n8位加法器_1_out_20 , \n8位加法器_1_out_21 , \n8位加法器_1_out_22 ,
       \n8位加法器_1_out_23 , \n8位加法器_1_out_24 , \n8位加法器_1_out_25 , \n8位加法器_1_out_26 , xor_1_out, \取反器_1_out_10 ,
       \取反器_1_out_11 , \取反器_1_out_12 , \取反器_1_out_13 , \取反器_1_out_14 , \取反器_1_out_15 , \取反器_1_out_16 ,
       \取反器_1_out_17 ;

  xor xor_1 (xor_1_out, \n8位加法器_1_out_24 , in_19);
  LED led_1 (.in(\n8位加法器_1_out_20 ));
  LED led_2 (.in(xor_1_out));
  \_8位加法器  \u_8位加法器_1  (
    .in_15(in_10), .in_16(\取反器_1_out_10 ), .in_5(in_11), .in_6(\取反器_1_out_11 ), .in_7(in_12),
    .in_8(\取反器_1_out_12 ), .in_9(in_13), .in_10(\取反器_1_out_13 ), .in_1(in_14), .in_11(\取反器_1_out_14 ),
    .in_12(in_15), .in_13(\取反器_1_out_15 ), .in_17(in_16), .in_14(\取反器_1_out_16 ), .in_2(in_17),
    .in_3(\取反器_1_out_17 ), .in_4(in_18), .out_24(\n8位加法器_1_out_24 ), .out_20(\n8位加法器_1_out_20 ),
    .out_21(\n8位加法器_1_out_21 ), .out_18(\n8位加法器_1_out_18 ), .out_19(\n8位加法器_1_out_19 ),
    .out_22(\n8位加法器_1_out_22 ), .out_23(\n8位加法器_1_out_23 ), .out_25(\n8位加法器_1_out_25 ),
    .out_26(\n8位加法器_1_out_26 ));
  LED led_3 (.in(\n8位加法器_1_out_21 ));
  LED led_4 (.in(\n8位加法器_1_out_18 ));
  \取反器  \u_取反器_1  (
    .out_10(\取反器_1_out_10 ), .out_11(\取反器_1_out_11 ), .out_12(\取反器_1_out_12 ), .out_13(\取反器_1_out_13 ),
    .out_14(\取反器_1_out_14 ), .out_15(\取反器_1_out_15 ), .out_16(\取反器_1_out_16 ), .out_17(\取反器_1_out_17 ),
    .in_1(in_1), .in_2(in_2), .in_3(in_3), .in_4(in_4), .in_5(in_5), .in_6(in_6), .in_7(in_7), .in_8(in_8),
    .in_9(in_9));
  LED led_5 (.in(\n8位加法器_1_out_23 ));
  LED led_6 (.in(\n8位加法器_1_out_19 ));
  LED led_7 (.in(\n8位加法器_1_out_22 ));
  LED led_8 (.in(\n8位加法器_1_out_26 ));
  LED led_9 (.in(\n8位加法器_1_out_25 ));
endmodule

module \半加器  (
  input  in_1,
  input  in_2,
  output out_3,
  output out_4
);

  xor xor_1 (out_3, in_1, in_2);
  and and_1 (out_4, in_1, in_2);
endmodule

module \_8位加法器  (
  input  in_1,
  input  in_2,
  input  in_3,
  input  in_4,
  input  in_5,
  input  in_6,
  input  in_7,
  input  in_8,
  input  in_9,
  input  in_10,
  input  in_11,
  input  in_12,
  input  in_13,
  input  in_14,
  input  in_15,
  input  in_16,
  input  in_17,
  output out_18,
  output out_19,
  output out_20,
  output out_21,
  output out_22,
  output out_23,
  output out_24,
  output out_25,
  output out_26
);

  wire \全加器_2_out_5 , \全加器_3_out_5 , \全加器_4_out_5 , \全加器_5_out_5 , \全加器_6_out_5 , \全加器_7_out_5 ,
       \全加器_8_out_5 ;

  \全加器  \u_全加器_1  (.in_1(\全加器_2_out_5 ), .in_2(in_15), .in_3(in_16), .out_4(out_20), .out_5(out_24));
  \全加器  \u_全加器_2  (.in_1(\全加器_3_out_5 ), .in_2(in_5), .in_3(in_6), .out_4(out_21), .out_5(\全加器_2_out_5 ));
  \全加器  \u_全加器_3  (.in_1(\全加器_4_out_5 ), .in_2(in_7), .in_3(in_8), .out_4(out_18), .out_5(\全加器_3_out_5 ));
  \全加器  \u_全加器_4  (.in_1(\全加器_5_out_5 ), .in_2(in_9), .in_3(in_10), .out_4(out_19), .out_5(\全加器_4_out_5 ));
  \全加器  \u_全加器_5  (.in_1(\全加器_6_out_5 ), .in_2(in_1), .in_3(in_11), .out_4(out_22), .out_5(\全加器_5_out_5 ));
  \全加器  \u_全加器_6  (.in_1(\全加器_7_out_5 ), .in_2(in_12), .in_3(in_13), .out_4(out_23), .out_5(\全加器_6_out_5 ));
  \全加器  \u_全加器_7  (.in_1(\全加器_8_out_5 ), .in_2(in_17), .in_3(in_14), .out_4(out_25), .out_5(\全加器_7_out_5 ));
  \全加器  \u_全加器_8  (.in_1(in_4), .in_2(in_2), .in_3(in_3), .out_4(out_26), .out_5(\全加器_8_out_5 ));
endmodule

module \取反器  (
  input  in_1,
  input  in_2,
  input  in_3,
  input  in_4,
  input  in_5,
  input  in_6,
  input  in_7,
  input  in_8,
  input  in_9,
  output out_10,
  output out_11,
  output out_12,
  output out_13,
  output out_14,
  output out_15,
  output out_16,
  output out_17
);

  xor xor_1 (out_10, in_9, in_1);
  xor xor_2 (out_11, in_9, in_2);
  xor xor_3 (out_12, in_9, in_3);
  xor xor_4 (out_13, in_9, in_4);
  xor xor_5 (out_14, in_9, in_5);
  xor xor_6 (out_15, in_9, in_6);
  xor xor_7 (out_16, in_9, in_7);
  xor xor_8 (out_17, in_9, in_8);
endmodule

module \R_S触发器  (
  input  R,
  input  S,
  output out_3,
  output out_4
);

  nor nor_1 (out_3, R, out_4);
  nor nor_2 (out_4, out_3, S);

  // Notes on the sheet:
  //   Q
  //   |Q
endmodule

module \振荡器  (
);

  wire clock_1_out, not_1_out;

  Clock clock_1 (.out(clock_1_out));
  // NOT_Gate not_1 has open pins: in=open, out=not_1_out
  LED led_1 (.in(clock_1_out));
endmodule

module \带清零D型锁存器  (
  input  \清零 ,
  input  \保持位_时钟 ,
  input  \数据端 ,
  output out_4,
  output out_5
);

  wire and_1_out, and_2_out, not_1_out, or_1_out;

  not not_1 (not_1_out, \数据端 );
  and and_1 (and_1_out, not_1_out, \保持位_时钟 );
  and and_2 (and_2_out, \保持位_时钟 , \数据端 );
  or or_1 (or_1_out, \清零 , and_1_out);
  nor nor_1 (out_4, or_1_out, out_5);
  nor nor_2 (out_5, out_4, and_2_out);

  // Notes on the sheet:
  //   Q
  //   ~Q
endmodule

module \_2_1选择器  (
  input  B,
  input  \选择端 ,
  input  A,
  output out_4
);

  wire and_1_out, and_2_out, not_1_out;

  not not_1 (not_1_out, \选择端 );
  and and_1 (and_1_out, B, \选择端 );
  and and_2 (and_2_out, not_1_out, A);
  or or_1 (out_4, and_1_out, and_2_out);
endmodule

module \边缘触发的D型触发器  (
  input  \数据端 ,
  input  \时钟 ,
  output Q,
  output nQ
);

  wire and_1_out, and_2_out, and_3_out, and_4_out, nor_1_out, nor_2_out, not_1_out, not_2_out;

  not not_1 (not_1_out, \数据端 );
  not not_2 (not_2_out, \时钟 );
  and and_1 (and_1_out, \数据端 , not_2_out);
  and and_2 (and_2_out, not_2_out, not_1_out);
  nor nor_1 (nor_1_out, and_1_out, nor_2_out);
  nor nor_2 (nor_2_out, nor_1_out, and_2_out);
  and and_3 (and_3_out, nor_1_out, \时钟 );
  and and_4 (and_4_out, \时钟 , nor_2_out);
  nor nor_3 (Q, and_3_out, nQ);
  nor nor_4 (nQ, Q, and_4_out);
endmodule

module test (
  input  in_1,
  input  in_2,
  input  in_3,
  input  in_4,
  input  in_5,
  input  c0,
  input  in_7,
  input  in_8
);

  wire clock_1_out, clock_2_out, not_1_out;
  wire [7:0] multiplexer_1_out, \n8位加法器_1_out_26 , ram_1_data, ram_2_data, \取反器_1_out_17 ,
       \带清零的边缘触发8位锁存器_1_out_18 , \边缘触发8位锁存器_1_out_17 , \边缘触发8位锁存器_2_out_17 , \边缘触发8位锁存器_3_out_17 ;
  wire [15:0] counter_1_q;

  Clock clock_1 (.out(clock_1_out));
  Counter #(.width(16), .max('hffff)) counter_1 (
    .Q(counter_1_q), .clk(clock_1_out), .clr(in_5));  // open: load, D, count, carry
  RAM #(.addrWidth(16), .bus("separate")) ram_1 (
    .addr(counter_1_q), .data(ram_1_data));  // open: din, str, sel, clk, ld, clr
  not not_1 (not_1_out, in_4);
  RAM #(.addrWidth(16), .bus("separate")) ram_2 (
    .addr(counter_1_q), .din(\带清零的边缘触发8位锁存器_1_out_18 ), .data(ram_2_data), .str(in_4), .ld(not_1_out));  // open: sel, clk, clr
  Multiplexer #(.width(8), .enable("false")) multiplexer_1 (
    .in0(ram_2_data), .in1(\n8位加法器_1_out_26 ), .out(multiplexer_1_out), .sel(in_7));
  \边缘触发8位锁存器  \u_边缘触发8位锁存器_1  (
    .in_9(in_1), .in_1(ram_1_data[7]), .in_2(ram_1_data[6]), .in_3(ram_1_data[5]), .in_4(ram_1_data[4]),
    .in_5(ram_1_data[3]), .in_6(ram_1_data[2]), .in_7(ram_1_data[1]), .in_8(ram_1_data[0]),
    .out_12(\边缘触发8位锁存器_1_out_17 [7]), .out_13(\边缘触发8位锁存器_1_out_17 [6]), .out_10(\边缘触发8位锁存器_1_out_17 [5]),
    .out_14(\边缘触发8位锁存器_1_out_17 [4]), .out_15(\边缘触发8位锁存器_1_out_17 [3]), .out_16(\边缘触发8位锁存器_1_out_17 [2]),
    .out_11(\边缘触发8位锁存器_1_out_17 [1]), .out_17(\边缘触发8位锁存器_1_out_17 [0]));
  \边缘触发8位锁存器  \u_边缘触发8位锁存器_2  (
    .in_9(in_2), .in_1(ram_1_data[7]), .in_2(ram_1_data[6]), .in_3(ram_1_data[5]), .in_4(ram_1_data[4]),
    .in_5(ram_1_data[3]), .in_6(ram_1_data[2]), .in_7(ram_1_data[1]), .in_8(ram_1_data[0]),
    .out_12(\边缘触发8位锁存器_2_out_17 [7]), .out_13(\边缘触发8位锁存器_2_out_17 [6]), .out_10(\边缘触发8位锁存器_2_out_17 [5]),
    .out_14(\边缘触发8位锁存器_2_out_17 [4]), .out_15(\边缘触发8位锁存器_2_out_17 [3]), .out_16(\边缘触发8位锁存器_2_out_17 [2]),
    .out_11(\边缘触发8位锁存器_2_out_17 [1]), .out_17(\边缘触发8位锁存器_2_out_17 [0]));
  \边缘触发8位锁存器  \u_边缘触发8位锁存器_3  (
    .in_9(in_3), .in_1(ram_1_data[7]), .in_2(ram_1_data[6]), .in_3(ram_1_data[5]), .in_4(ram_1_data[4]),
    .in_5(ram_1_data[3]), .in_6(ram_1_data[2]), .in_7(ram_1_data[1]), .in_8(ram_1_data[0]),
    .out_12(\边缘触发8位锁存器_3_out_17 [7]), .out_13(\边缘触发8位锁存器_3_out_17 [6]), .out_10(\边缘触发8位锁存器_3_out_17 [5]),
    .out_14(\边缘触发8位锁存器_3_out_17 [4]), .out_15(\边缘触发8位锁存器_3_out_17 [3]), .out_16(\边缘触发8位锁存器_3_out_17 [2]),
    .out_11(\边缘触发8位锁存器_3_out_17 [1]), .out_17(\边缘触发8位锁存器_3_out_17 [0]));
  \取反器  \u_取反器_1  (
    .out_10(\取反器_1_out_17 [7]), .out_11(\取反器_1_out_17 [6]), .out_12(\取反器_1_out_17 [5]),
    .out_13(\取反器_1_out_17 [4]), .out_14(\取反器_1_out_17 [3]), .out_15(\取反器_1_out_17 [2]),
    .out_16(\取反器_1_out_17 [1]), .out_17(\取反器_1_out_17 [0]), .in_1(ram_2_data[7]), .in_2(ram_2_data[6]),
    .in_3(ram_2_data[5]), .in_4(ram_2_data[4]), .in_5(ram_2_data[3]), .in_6(ram_2_data[2]),
    .in_7(ram_2_data[1]), .in_8(ram_2_data[0]), .in_9(c0));
  \_8位加法器  \u_8位加法器_1  (
    .in_15(\取反器_1_out_17 [7]), .in_16(\带清零的边缘触发8位锁存器_1_out_18 [7]), .in_5(\取反器_1_out_17 [6]),
    .in_6(\带清零的边缘触发8位锁存器_1_out_18 [6]), .in_7(\取反器_1_out_17 [5]), .in_8(\带清零的边缘触发8位锁存器_1_out_18 [5]),
    .in_9(\取反器_1_out_17 [4]), .in_10(\带清零的边缘触发8位锁存器_1_out_18 [4]), .in_1(\取反器_1_out_17 [3]),
    .in_11(\带清零的边缘触发8位锁存器_1_out_18 [3]), .in_12(\取反器_1_out_17 [2]), .in_13(\带清零的边缘触发8位锁存器_1_out_18 [2]),
    .in_17(\取反器_1_out_17 [1]), .in_14(\带清零的边缘触发8位锁存器_1_out_18 [1]), .in_2(\取反器_1_out_17 [0]),
    .in_3(\带清零的边缘触发8位锁存器_1_out_18 [0]), .in_4(c0), .out_20(\n8位加法器_1_out_26 [7]),
    .out_21(\n8位加法器_1_out_26 [6]), .out_18(\n8位加法器_1_out_26 [5]), .out_19(\n8位加法器_1_out_26 [4]),
    .out_22(\n8位加法器_1_out_26 [3]), .out_23(\n8位加法器_1_out_26 [2]), .out_25(\n8位加法器_1_out_26 [1]),
    .out_26(\n8位加法器_1_out_26 [0]));  // open: out_24
  \带清零的边缘触发8位锁存器  \u_带清零的边缘触发8位锁存器_1  (
    .\清零 (in_8), .in_10(clock_2_out), .in_1(multiplexer_1_out[7]), .in_2(multiplexer_1_out[6]),
    .in_3(multiplexer_1_out[5]), .in_4(multiplexer_1_out[4]), .in_5(multiplexer_1_out[3]),
    .in_6(multiplexer_1_out[2]), .in_7(multiplexer_1_out[1]), .in_8(multiplexer_1_out[0]),
    .out_13(\带清零的边缘触发8位锁存器_1_out_18 [7]), .out_14(\带清零的边缘触发8位锁存器_1_out_18 [6]),
    .out_11(\带清零的边缘触发8位锁存器_1_out_18 [5]), .out_15(\带清零的边缘触发8位锁存器_1_out_18 [4]),
    .out_16(\带清零的边缘触发8位锁存器_1_out_18 [3]), .out_17(\带清零的边缘触发8位锁存器_1_out_18 [2]),
    .out_12(\带清零的边缘触发8位锁存器_1_out_18 [1]), .out_18(\带清零的边缘触发8位锁存器_1_out_18 [0]));
  LED led_1 (.in(\带清零的边缘触发8位锁存器_1_out_18 [0]));
  LED led_2 (.in(\带清零的边缘触发8位锁存器_1_out_18 [1]));
  LED led_3 (.in(\带清零的边缘触发8位锁存器_1_out_18 [2]));
  LED led_4 (.in(\带清零的边缘触发8位锁存器_1_out_18 [3]));
  LED led_5 (.in(\带清零的边缘触发8位锁存器_1_out_18 [4]));
  LED led_6 (.in(\带清零的边缘触发8位锁存器_1_out_18 [5]));
  LED led_7 (.in(\带清零的边缘触发8位锁存器_1_out_18 [6]));
  LED led_8 (.in(\带清零的边缘触发8位锁存器_1_out_18 [7]));
  Clock clock_2 (.out(clock_2_out));

  // Notes on the sheet:
  //   代码
  //   数据
  //   1
  //   2
  //   4
  //   8
  //   16
  //   32
  //   64
  //   128
endmodule

module \_8位波形计数器  (
  output out_1,
  output out_2,
  output out_3,
  output out_4,
  output out_5,
  output out_6,
  output out_7,
  output out_8,
  output out_9
);

  wire clock_1_out, \边缘触发的d型触发器_1_nq , \边缘触发的d型触发器_2_nq , \边缘触发的d型触发器_3_nq , \边缘触发的d型触发器_4_nq ,
       \边缘触发的d型触发器_5_nq , \边缘触发的d型触发器_6_nq , \边缘触发的d型触发器_7_nq , \边缘触发的d型触发器_8_nq ;

  Clock clock_1 (.out(clock_1_out));
  not not_1 (out_1, clock_1_out);
  \边缘触发的D型触发器  \u_边缘触发的d型触发器_1  (.\数据端 (\边缘触发的d型触发器_1_nq ), .\时钟 (clock_1_out), .Q(out_2), .nQ(\边缘触发的d型触发器_1_nq ));
  \边缘触发的D型触发器  \u_边缘触发的d型触发器_2  (
    .\数据端 (\边缘触发的d型触发器_2_nq ), .\时钟 (\边缘触发的d型触发器_1_nq ), .Q(out_5), .nQ(\边缘触发的d型触发器_2_nq ));
  \边缘触发的D型触发器  \u_边缘触发的d型触发器_3  (
    .\数据端 (\边缘触发的d型触发器_3_nq ), .\时钟 (\边缘触发的d型触发器_2_nq ), .Q(out_6), .nQ(\边缘触发的d型触发器_3_nq ));
  \边缘触发的D型触发器  \u_边缘触发的d型触发器_4  (
    .\数据端 (\边缘触发的d型触发器_4_nq ), .\时钟 (\边缘触发的d型触发器_3_nq ), .Q(out_3), .nQ(\边缘触发的d型触发器_4_nq ));
  \边缘触发的D型触发器  \u_边缘触发的d型触发器_5  (
    .\数据端 (\边缘触发的d型触发器_5_nq ), .\时钟 (\边缘触发的d型触发器_4_nq ), .Q(out_7), .nQ(\边缘触发的d型触发器_5_nq ));
  \边缘触发的D型触发器  \u_边缘触发的d型触发器_6  (
    .\数据端 (\边缘触发的d型触发器_6_nq ), .\时钟 (\边缘触发的d型触发器_5_nq ), .Q(out_8), .nQ(\边缘触发的d型触发器_6_nq ));
  \边缘触发的D型触发器  \u_边缘触发的d型触发器_7  (
    .\数据端 (\边缘触发的d型触发器_7_nq ), .\时钟 (\边缘触发的d型触发器_6_nq ), .Q(out_4), .nQ(\边缘触发的d型触发器_7_nq ));
  \边缘触发的D型触发器  \u_边缘触发的d型触发器_8  (
    .\数据端 (\边缘触发的d型触发器_8_nq ), .\时钟 (\边缘触发的d型触发器_7_nq ), .Q(out_9), .nQ(\边缘触发的d型触发器_8_nq ));
endmodule

module \带预置与清零的边缘型D锁存器  (
  input  \清零 ,
  input  \预置 ,
  input  \时钟 ,
  input  D,
  output Q,
  output nQ
);

  wire nor_1_out, nor_2_out, nor_3_out, nor_4_out, not_1_out;

  not not_1 (not_1_out, \时钟 );
  nor nor_1 (nor_1_out, \清零 , nor_4_out, nor_2_out);
  nor nor_2 (nor_2_out, nor_1_out, \预置 , not_1_out);
  nor nor_3 (nor_3_out, nor_2_out, not_1_out, nor_4_out);
  nor nor_4 (nor_4_out, nor_3_out, \预置 , D);
  nor nor_5 (Q, \清零 , nor_2_out, nQ);
  nor nor_6 (nQ, Q, \预置 , nor_3_out);
endmodule

module \_1位锁存器  (
  input  \写操作端 ,
  input  \数据输入 ,
  output out_3
);

  wire and_1_out, and_2_out, nor_2_out, not_1_out;

  not not_1 (not_1_out, \数据输入 );
  and and_1 (and_1_out, not_1_out, \写操作端 );
  and and_2 (and_2_out, \写操作端 , \数据输入 );
  nor nor_1 (out_3, and_1_out, nor_2_out);
  nor nor_2 (nor_2_out, out_3, and_2_out);

  // Notes on the sheet:
  //   数据输出
endmodule

module \_8位锁存器  (
  input  in_1,
  input  in_2,
  input  in_3,
  input  in_4,
  input  in_5,
  input  in_6,
  input  in_7,
  input  in_8,
  input  in_9,
  output out_10,
  output out_11,
  output out_12,
  output out_13,
  output out_14,
  output out_15,
  output out_16,
  output out_17
);

  \_1位锁存器  \u_1位锁存器_1  (.\写操作端 (in_9), .\数据输入 (in_2), .out_3(out_13));
  \_1位锁存器  \u_1位锁存器_2  (.\写操作端 (in_9), .\数据输入 (in_1), .out_3(out_12));
  \_1位锁存器  \u_1位锁存器_3  (.\写操作端 (in_9), .\数据输入 (in_3), .out_3(out_10));
  \_1位锁存器  \u_1位锁存器_4  (.\写操作端 (in_9), .\数据输入 (in_4), .out_3(out_14));
  \_1位锁存器  \u_1位锁存器_5  (.\写操作端 (in_9), .\数据输入 (in_8), .out_3(out_15));
  \_1位锁存器  \u_1位锁存器_6  (.\写操作端 (in_9), .\数据输入 (in_5), .out_3(out_16));
  \_1位锁存器  \u_1位锁存器_7  (.\写操作端 (in_9), .\数据输入 (in_6), .out_3(out_11));
  \_1位锁存器  \u_1位锁存器_8  (.\写操作端 (in_9), .\数据输入 (in_7), .out_3(out_17));
endmodule

module \_8_1选择器  (
  input  in_1,
  input  in_2,
  input  in_3,
  input  in_4,
  input  in_5,
  input  in_6,
  input  in_7,
  input  in_8,
  input  in_9,
  input  in_10,
  input  in_11,
  output \数据输出 
);

  wire and_1_out, and_2_out, and_3_out, and_4_out, and_5_out, and_6_out, and_7_out, and_8_out, not_1_out,
       not_2_out, not_3_out;

  not not_1 (not_1_out, in_9);
  not not_2 (not_2_out, in_10);
  not not_3 (not_3_out, in_11);
  and and_1 (and_1_out, in_1, not_1_out, not_2_out, not_3_out);
  and and_2 (and_2_out, in_2, in_9, not_2_out, not_3_out);
  and and_3 (and_3_out, in_3, in_10, not_1_out, not_3_out);
  and and_4 (and_4_out, in_4, in_9, in_10, not_3_out);
  and and_5 (and_5_out, in_5, in_11, not_1_out, not_2_out);
  and and_6 (and_6_out, in_6, in_9, in_11, not_2_out);
  and and_7 (and_7_out, in_7, in_10, in_11, not_1_out);
  and and_8 (and_8_out, in_8, in_9, in_10, in_11);
  or or_1 (\数据输出 , and_1_out, and_2_out, and_3_out, and_4_out, and_5_out, and_6_out, and_7_out, and_8_out);
endmodule

module \_3_8译码器  (
  input  in_1,
  input  in_2,
  input  in_3,
  input  in_4,
  output out_5,
  output out_6,
  output out_7,
  output out_8,
  output out_9,
  output out_10,
  output out_11,
  output out_12
);

  wire not_1_out, not_2_out, not_3_out;

  not not_1 (not_1_out, in_2);
  not not_2 (not_2_out, in_3);
  not not_3 (not_3_out, in_4);
  and and_1 (out_5, in_1, not_1_out, not_2_out, not_3_out);
  and and_2 (out_6, in_1, in_2, not_2_out, not_3_out);
  and and_3 (out_7, in_1, in_3, not_1_out, not_3_out);
  and and_4 (out_8, in_1, in_2, in_3, not_3_out);
  and and_5 (out_9, in_1, in_4, not_1_out, not_2_out);
  and and_6 (out_10, in_1, in_2, in_4, not_2_out);
  and and_7 (out_11, in_1, in_3, in_4, not_1_out);
  and and_8 (out_12, in_1, in_2, in_3, in_4);
endmodule

module \随机访问存储器  (
  input  in_1,
  input  in_2,
  input  \地址端口 ,
  input  \写操作端 ,
  input  \数据输入 ,
  output \数据输出 
);

  wire \n1位锁存器_1_out_3 , \n1位锁存器_2_out_3 , \n1位锁存器_3_out_3 , \n1位锁存器_4_out_3 , \n1位锁存器_5_out_3 ,
       \n1位锁存器_6_out_3 , \n1位锁存器_7_out_3 , \n1位锁存器_8_out_3 , \n3_8译码器_1_out_5 , \n3_8译码器_1_out_6 ,
       \n3_8译码器_1_out_7 , \n3_8译码器_1_out_8 , \n3_8译码器_1_out_9 , \n3_8译码器_1_out_10 , \n3_8译码器_1_out_11 ,
       \n3_8译码器_1_out_12 ;

  \_1位锁存器  \u_1位锁存器_1  (.\写操作端 (\n3_8译码器_1_out_12 ), .\数据输入 (\数据输入 ), .out_3(\n1位锁存器_1_out_3 ));
  \_1位锁存器  \u_1位锁存器_2  (.\写操作端 (\n3_8译码器_1_out_10 ), .\数据输入 (\数据输入 ), .out_3(\n1位锁存器_2_out_3 ));
  \_1位锁存器  \u_1位锁存器_3  (.\写操作端 (\n3_8译码器_1_out_11 ), .\数据输入 (\数据输入 ), .out_3(\n1位锁存器_3_out_3 ));
  \_3_8译码器  \u_3_8译码器_1  (
    .in_1(\写操作端 ), .in_2(in_2), .in_3(in_1), .in_4(\地址端口 ), .out_5(\n3_8译码器_1_out_5 ),
    .out_6(\n3_8译码器_1_out_6 ), .out_7(\n3_8译码器_1_out_7 ), .out_8(\n3_8译码器_1_out_8 ),
    .out_9(\n3_8译码器_1_out_9 ), .out_10(\n3_8译码器_1_out_10 ), .out_11(\n3_8译码器_1_out_11 ),
    .out_12(\n3_8译码器_1_out_12 ));
  \_1位锁存器  \u_1位锁存器_4  (.\写操作端 (\n3_8译码器_1_out_9 ), .\数据输入 (\数据输入 ), .out_3(\n1位锁存器_4_out_3 ));
  \_1位锁存器  \u_1位锁存器_5  (.\写操作端 (\n3_8译码器_1_out_8 ), .\数据输入 (\数据输入 ), .out_3(\n1位锁存器_5_out_3 ));
  \_8_1选择器  \u_8_1选择器_1  (
    .in_1(\n1位锁存器_8_out_3 ), .in_2(\n1位锁存器_7_out_3 ), .in_3(\n1位锁存器_6_out_3 ), .in_4(\n1位锁存器_5_out_3 ),
    .in_5(\n1位锁存器_4_out_3 ), .in_6(\n1位锁存器_2_out_3 ), .in_7(\n1位锁存器_3_out_3 ), .in_8(\n1位锁存器_1_out_3 ),
    .in_9(in_2), .in_10(in_1), .in_11(\地址端口 ), .\数据输出 (\数据输出 ));
  \_1位锁存器  \u_1位锁存器_6  (.\写操作端 (\n3_8译码器_1_out_7 ), .\数据输入 (\数据输入 ), .out_3(\n1位锁存器_6_out_3 ));
  \_1位锁存器  \u_1位锁存器_7  (.\写操作端 (\n3_8译码器_1_out_6 ), .\数据输入 (\数据输入 ), .out_3(\n1位锁存器_7_out_3 ));
  \_1位锁存器  \u_1位锁存器_8  (.\写操作端 (\n3_8译码器_1_out_5 ), .\数据输入 (\数据输入 ), .out_3(\n1位锁存器_8_out_3 ));
endmodule

module \带清零的8位锁存器  (
  input  in_1,
  input  in_2,
  input  in_3,
  input  in_4,
  input  in_5,
  input  in_6,
  input  in_7,
  input  in_8,
  input  \清零 ,
  input  in_10,
  output out_11,
  output out_12,
  output out_13,
  output out_14,
  output out_15,
  output out_16,
  output out_17,
  output out_18
);

  wire and_1_out, and_2_out, and_3_out, and_4_out, and_5_out, and_6_out, and_7_out, and_8_out, not_1_out,
       or_1_out;

  not not_1 (not_1_out, \清零 );
  or or_1 (or_1_out, \清零 , in_10);
  and and_1 (and_1_out, not_1_out, in_1);
  and and_2 (and_2_out, not_1_out, in_2);
  \_1位锁存器  \u_1位锁存器_1  (.\写操作端 (or_1_out), .\数据输入 (and_1_out), .out_3(out_13));
  and and_3 (and_3_out, not_1_out, in_3);
  \_1位锁存器  \u_1位锁存器_2  (.\写操作端 (or_1_out), .\数据输入 (and_3_out), .out_3(out_11));
  \_1位锁存器  \u_1位锁存器_3  (.\写操作端 (or_1_out), .\数据输入 (and_2_out), .out_3(out_14));
  and and_4 (and_4_out, not_1_out, in_4);
  \_1位锁存器  \u_1位锁存器_4  (.\写操作端 (or_1_out), .\数据输入 (and_4_out), .out_3(out_15));
  and and_5 (and_5_out, not_1_out, in_6);
  and and_6 (and_6_out, not_1_out, in_5);
  \_1位锁存器  \u_1位锁存器_5  (.\写操作端 (or_1_out), .\数据输入 (and_5_out), .out_3(out_17));
  \_1位锁存器  \u_1位锁存器_6  (.\写操作端 (or_1_out), .\数据输入 (and_6_out), .out_3(out_16));
  and and_7 (and_7_out, not_1_out, in_7);
  \_1位锁存器  \u_1位锁存器_7  (.\写操作端 (or_1_out), .\数据输入 (and_7_out), .out_3(out_12));
  \_1位锁存器  \u_1位锁存器_8  (.\写操作端 (or_1_out), .\数据输入 (and_8_out), .out_3(out_18));
  and and_8 (and_8_out, in_8, not_1_out);

  // Notes on the sheet:
  //   时钟
endmodule

module \边缘触发1位锁存器  (
  input  \数据输入 ,
  input  \写操作端 ,
  output \数据输出 
);

  wire and_1_out, and_2_out, and_3_out, and_4_out, nor_1_out, nor_2_out, nor_4_out, not_1_out, not_2_out;

  not not_1 (not_1_out, \数据输入 );
  not not_2 (not_2_out, \写操作端 );
  and and_1 (and_1_out, \数据输入 , not_2_out);
  and and_2 (and_2_out, not_2_out, not_1_out);
  nor nor_1 (nor_1_out, and_1_out, nor_2_out);
  nor nor_2 (nor_2_out, nor_1_out, and_2_out);
  and and_3 (and_3_out, nor_1_out, \写操作端 );
  and and_4 (and_4_out, \写操作端 , nor_2_out);
  nor nor_3 (\数据输出 , and_3_out, nor_4_out);
  nor nor_4 (nor_4_out, \数据输出 , and_4_out);
endmodule

module \带清零的边缘触发8位锁存器  (
  input  in_1,
  input  in_2,
  input  in_3,
  input  in_4,
  input  in_5,
  input  in_6,
  input  in_7,
  input  in_8,
  input  \清零 ,
  input  in_10,
  output out_11,
  output out_12,
  output out_13,
  output out_14,
  output out_15,
  output out_16,
  output out_17,
  output out_18
);

  wire and_1_out, and_2_out, and_3_out, and_4_out, and_5_out, and_6_out, and_7_out, and_8_out, not_1_out,
       or_1_out;

  not not_1 (not_1_out, \清零 );
  buf or_1 (or_1_out, in_10);  // OR_Gate
  and and_1 (and_1_out, not_1_out, in_2);
  and and_2 (and_2_out, not_1_out, in_1);
  \边缘触发1位锁存器  \u_边缘触发1位锁存器_1  (.\数据输入 (and_2_out), .\写操作端 (or_1_out), .\数据输出 (out_13));
  and and_3 (and_3_out, not_1_out, in_3);
  \边缘触发1位锁存器  \u_边缘触发1位锁存器_2  (.\数据输入 (and_3_out), .\写操作端 (or_1_out), .\数据输出 (out_11));
  \边缘触发1位锁存器  \u_边缘触发1位锁存器_3  (.\数据输入 (and_1_out), .\写操作端 (or_1_out), .\数据输出 (out_14));
  and and_4 (and_4_out, not_1_out, in_4);
  \边缘触发1位锁存器  \u_边缘触发1位锁存器_4  (.\数据输入 (and_4_out), .\写操作端 (or_1_out), .\数据输出 (out_15));
  and and_5 (and_5_out, not_1_out, in_6);
  and and_6 (and_6_out, not_1_out, in_5);
  \边缘触发1位锁存器  \u_边缘触发1位锁存器_5  (.\数据输入 (and_6_out), .\写操作端 (or_1_out), .\数据输出 (out_16));
  \边缘触发1位锁存器  \u_边缘触发1位锁存器_6  (.\数据输入 (and_5_out), .\写操作端 (or_1_out), .\数据输出 (out_17));
  and and_7 (and_7_out, not_1_out, in_7);
  \边缘触发1位锁存器  \u_边缘触发1位锁存器_7  (.\数据输入 (and_7_out), .\写操作端 (or_1_out), .\数据输出 (out_12));
  \边缘触发1位锁存器  \u_边缘触发1位锁存器_8  (.\数据输入 (and_8_out), .\写操作端 (or_1_out), .\数据输出 (out_18));
  and and_8 (and_8_out, in_8, not_1_out);

  // Notes on the sheet:
  //   时钟
endmodule

module \边缘触发8位锁存器  (
  input  in_1,
  input  in_2,
  input  in_3,
  input  in_4,
  input  in_5,
  input  in_6,
  input  in_7,
  input  in_8,
  input  in_9,
  output out_10,
  output out_11,
  output out_12,
  output out_13,
  output out_14,
  output out_15,
  output out_16,
  output out_17
);

  wire or_1_out;

  buf or_1 (or_1_out, in_9);  // OR_Gate
  \边缘触发1位锁存器  \u_边缘触发1位锁存器_1  (.\数据输入 (in_1), .\写操作端 (or_1_out), .\数据输出 (out_12));
  \边缘触发1位锁存器  \u_边缘触发1位锁存器_2  (.\数据输入 (in_2), .\写操作端 (or_1_out), .\数据输出 (out_13));
  \边缘触发1位锁存器  \u_边缘触发1位锁存器_3  (.\数据输入 (in_3), .\写操作端 (or_1_out), .\数据输出 (out_10));
  \边缘触发1位锁存器  \u_边缘触发1位锁存器_4  (.\数据输入 (in_4), .\写操作端 (or_1_out), .\数据输出 (out_14));
  \边缘触发1位锁存器  \u_边缘触发1位锁存器_5  (.\数据输入 (in_5), .\写操作端 (or_1_out), .\数据输出 (out_15));
  \边缘触发1位锁存器  \u_边缘触发1位锁存器_6  (.\数据输入 (in_6), .\写操作端 (or_1_out), .\数据输出 (out_16));
  \边缘触发1位锁存器  \u_边缘触发1位锁存器_7  (.\数据输入 (in_7), .\写操作端 (or_1_out), .\数据输出 (out_11));
  \边缘触发1位锁存器  \u_边缘触发1位锁存器_8  (.\数据输入 (in_8), .\写操作端 (or_1_out), .\数据输出 (out_17));

  // Notes on the sheet:
  //   时钟
endmodule

module test2 (
  input  in_1,
  input  \置位 ,
  input  \复位 ,
  input  in_4,
  input  in_5,
  input  in_6,
  input  in_7,
  input  in_8
);

  wire \n16位计数器_1_p2 , undriven_2, undriven_4;
  wire [7:0] \n16位计数器_1_p4 , \n16位计数器_1_p4_2 , ram_1_data, ram_2_data, undriven, undriven_3,
       \边缘触发8位锁存器_1_out_17 ;
  wire [15:0] multiplexer_1_out, \n16位计数器_1_p5 ;

  // _16位计数器 16位计数器_1: pin names not known; wires that end beside it: \复位 , \n16位计数器_1_p2 , \置位 , {\n16位计数器_1_p4_2 , \n16位计数器_1_p4 }, \n16位计数器_1_p5 
  Clock clock_1 (.out(\n16位计数器_1_p2 ));
  Multiplexer #(.width(16), .enable("false")) multiplexer_1 (
    .in0(\n16位计数器_1_p5 ), .in1({\n16位计数器_1_p4_2 , \n16位计数器_1_p4 }), .out(multiplexer_1_out), .sel(in_5));
  RAM #(.addrWidth(16), .bus("separate")) ram_1 (
    .addr(multiplexer_1_out), .din(undriven), .data(ram_1_data), .str(undriven_2), .ld(in_6));  // open: sel, clk, clr
  \边缘触发8位锁存器  \u_边缘触发8位锁存器_1  (
    .in_9(in_1), .in_1(ram_1_data[7]), .in_2(ram_1_data[6]), .in_3(ram_1_data[5]), .in_4(ram_1_data[4]),
    .in_5(ram_1_data[3]), .in_6(ram_1_data[2]), .in_7(ram_1_data[1]), .in_8(ram_1_data[0]),
    .out_12(\边缘触发8位锁存器_1_out_17 [7]), .out_13(\边缘触发8位锁存器_1_out_17 [6]), .out_10(\边缘触发8位锁存器_1_out_17 [5]),
    .out_14(\边缘触发8位锁存器_1_out_17 [4]), .out_15(\边缘触发8位锁存器_1_out_17 [3]), .out_16(\边缘触发8位锁存器_1_out_17 [2]),
    .out_11(\边缘触发8位锁存器_1_out_17 [1]), .out_17(\边缘触发8位锁存器_1_out_17 [0]));
  \边缘触发8位锁存器  \u_边缘触发8位锁存器_2  (
    .in_9(in_4), .in_1(ram_1_data[7]), .in_2(ram_1_data[6]), .in_3(ram_1_data[5]), .in_4(ram_1_data[4]),
    .in_5(ram_1_data[3]), .in_6(ram_1_data[2]), .in_7(ram_1_data[1]), .in_8(ram_1_data[0]),
    .out_12(\n16位计数器_1_p4 [7]), .out_13(\n16位计数器_1_p4 [6]), .out_10(\n16位计数器_1_p4 [5]),
    .out_14(\n16位计数器_1_p4 [4]), .out_15(\n16位计数器_1_p4 [3]), .out_16(\n16位计数器_1_p4 [2]),
    .out_11(\n16位计数器_1_p4 [1]), .out_17(\n16位计数器_1_p4 [0]));
  \边缘触发8位锁存器  \u_边缘触发8位锁存器_3  (
    .in_9(in_8), .in_1(ram_1_data[7]), .in_2(ram_1_data[6]), .in_3(ram_1_data[5]), .in_4(ram_1_data[4]),
    .in_5(ram_1_data[3]), .in_6(ram_1_data[2]), .in_7(ram_1_data[1]), .in_8(ram_1_data[0]),
    .out_12(\n16位计数器_1_p4_2 [7]), .out_13(\n16位计数器_1_p4_2 [6]), .out_10(\n16位计数器_1_p4_2 [5]),
    .out_14(\n16位计数器_1_p4_2 [4]), .out_15(\n16位计数器_1_p4_2 [3]), .out_16(\n16位计数器_1_p4_2 [2]),
    .out_11(\n16位计数器_1_p4_2 [1]), .out_17(\n16位计数器_1_p4_2 [0]));
  RAM #(.addrWidth(16), .bus("separate")) ram_2 (
    .addr({\n16位计数器_1_p4_2 , \n16位计数器_1_p4 }), .din(undriven_3), .data(ram_2_data), .str(undriven_4),
    .ld(in_7));  // open: sel, clk, clr

  // Notes on the sheet:
  //   数据
  //   代码
endmodule

module \_1位D型边沿触发器  (
  input  \置位 ,
  input  A,
  input  \复位 ,
  output out_4
);

  wire and_1_out, and_2_out, not_1_out, or_1_out, undriven, undriven_2;

  not not_1 (not_1_out, A);
  and and_1 (and_1_out, \置位 , A);
  and and_2 (and_2_out, \置位 , not_1_out);
  or or_1 (or_1_out, and_2_out, \复位 );
  \带预置与清零的边缘型D锁存器  \u_带预置与清零的边缘型d锁存器_1  (
    .\清零 (or_1_out), .\预置 (and_1_out), .\时钟 (undriven_2), .D(undriven), .Q(out_4));  // open: nQ
endmodule

module \_16位D型边沿触发器  (
  input  \复位 ,
  input  in_2,
  input  in_3,
  input  in_4,
  input  in_5,
  input  in_6,
  input  in_7,
  input  in_8,
  input  in_9,
  input  in_10,
  input  in_11,
  input  in_12,
  input  in_13,
  input  in_14,
  input  in_15,
  input  in_16,
  input  in_17,
  input  \置位 ,
  output out_19,
  output out_20,
  output out_21,
  output out_22,
  output out_23,
  output out_24,
  output out_25,
  output out_26,
  output out_27,
  output out_28,
  output out_29,
  output out_30,
  output out_31,
  output out_32,
  output out_33,
  output out_34
);

  \_1位D型边沿触发器  \u_1位d型边沿触发器_1  (.A(in_3), .out_4(out_19), .\置位 (\置位 ), .\复位 (\复位 ));
  \_1位D型边沿触发器  \u_1位d型边沿触发器_2  (.A(in_4), .out_4(out_20), .\置位 (\置位 ), .\复位 (\复位 ));
  \_1位D型边沿触发器  \u_1位d型边沿触发器_3  (.A(in_5), .out_4(out_21), .\置位 (\置位 ), .\复位 (\复位 ));
  \_1位D型边沿触发器  \u_1位d型边沿触发器_4  (.A(in_6), .out_4(out_33), .\置位 (\置位 ), .\复位 (\复位 ));
  \_1位D型边沿触发器  \u_1位d型边沿触发器_5  (.A(in_7), .out_4(out_22), .\置位 (\置位 ), .\复位 (\复位 ));
  \_1位D型边沿触发器  \u_1位d型边沿触发器_6  (.A(in_15), .out_4(out_24), .\置位 (\置位 ), .\复位 (\复位 ));
  \_1位D型边沿触发器  \u_1位d型边沿触发器_7  (.A(in_14), .out_4(out_23), .\置位 (\置位 ), .\复位 (\复位 ));
  \_1位D型边沿触发器  \u_1位d型边沿触发器_8  (.A(in_8), .out_4(out_34), .\置位 (\置位 ), .\复位 (\复位 ));
  \_1位D型边沿触发器  \u_1位d型边沿触发器_9  (.A(in_9), .out_4(out_25), .\置位 (\置位 ), .\复位 (\复位 ));
  \_1位D型边沿触发器  \u_1位d型边沿触发器_10  (.A(in_17), .out_4(out_27), .\置位 (\置位 ), .\复位 (\复位 ));
  \_1位D型边沿触发器  \u_1位d型边沿触发器_11  (.A(in_16), .out_4(out_26), .\置位 (\置位 ), .\复位 (\复位 ));
  \_1位D型边沿触发器  \u_1位d型边沿触发器_12  (.A(in_10), .out_4(out_28), .\置位 (\置位 ), .\复位 (\复位 ));
  \_1位D型边沿触发器  \u_1位d型边沿触发器_13  (.A(in_2), .out_4(out_29), .\置位 (\置位 ), .\复位 (\复位 ));
  \_1位D型边沿触发器  \u_1位d型边沿触发器_14  (.A(in_12), .out_4(out_31), .\置位 (\置位 ), .\复位 (\复位 ));
  \_1位D型边沿触发器  \u_1位d型边沿触发器_15  (.A(in_11), .out_4(out_30), .\置位 (\置位 ), .\复位 (\复位 ));
  \_1位D型边沿触发器  \u_1位d型边沿触发器_16  (.A(in_13), .out_4(out_32), .\置位 (\置位 ), .\复位 (\复位 ));
endmodule

module \_16位计数器  (
  input  in_1,
  input  [15:0] in_2,
  input  in_3,
  input  in_4,
  input  in_5,
  output [15:0] out_6
);

  Counter #(.width(16), .max('hffff)) counter_1 (
    .load(in_1), .D(in_2), .count(in_3), .Q(out_6), .clk(in_4), .clr(in_5));  // open: carry
endmodule

module \自动加法器  (
  input  in_1,
  input  \操作台 ,
  input  in_3,
  input  in_4,
  input  in_5,
  input  in_6,
  input  in_7,
  input  in_8,
  input  in_9,
  input  in_10,
  input  in_11,
  input  in_12,
  input  in_13,
  output [7:0] \结果 
);

  wire clock_1_out, \n8位加法器_1_p7 , \n8位加法器_1_p10 , \n8位加法器_1_p12 , \n8位加法器_1_p13 , \n8位加法器_1_p14 ,
       \n8位加法器_1_p15 , \n8位加法器_1_p18 , \n8位加法器_1_p21 , not_1_out, not_2_out;
  wire [7:0] multiplexer_1_out, ram_1_data, \带清零的8位锁存器_1_out_18 ;
  wire [15:0] counter_1_q;

  Clock clock_1 (.out(clock_1_out));
  Counter #(.width(16), .max('hffff)) counter_1 (
    .Q(counter_1_q), .clk(clock_1_out), .clr(in_13));  // open: load, D, count, carry
  not not_1 (not_1_out, in_11);
  \带清零的8位锁存器  \u_带清零的8位锁存器_1  (
    .\清零 (in_9), .in_10(in_10), .in_1(in_1), .in_2(\操作台 ), .in_3(in_3), .in_4(in_4), .in_5(in_5),
    .in_6(in_6), .in_7(in_7), .in_8(in_8), .out_13(\带清零的8位锁存器_1_out_18 [7]),
    .out_14(\带清零的8位锁存器_1_out_18 [6]), .out_11(\带清零的8位锁存器_1_out_18 [5]), .out_15(\带清零的8位锁存器_1_out_18 [4]),
    .out_16(\带清零的8位锁存器_1_out_18 [3]), .out_17(\带清零的8位锁存器_1_out_18 [2]), .out_12(\带清零的8位锁存器_1_out_18 [1]),
    .out_18(\带清零的8位锁存器_1_out_18 [0]));
  not not_2 (not_2_out, not_1_out);
  RAM #(.addrWidth(16), .bus("separate")) ram_1 (
    .addr(counter_1_q), .din(\带清零的8位锁存器_1_out_18 ), .data(ram_1_data), .str(not_1_out), .clk(in_10),
    .ld(not_2_out));  // open: sel, clr
  Multiplexer #(.width(8), .enable("false")) multiplexer_1 (
    .in1(ram_1_data), .out(multiplexer_1_out), .sel(in_11));  // open: in0
  // _8位加法器 8位加法器_1: pin names not known; wires that end beside it: multiplexer_1_out, multiplexer_1_out[7], multiplexer_1_out[6], multiplexer_1_out[5], multiplexer_1_out[4], multiplexer_1_out[3], \n8位加法器_1_p7 , multiplexer_1_out[2], multiplexer_1_out[1], \n8位加法器_1_p10 , multiplexer_1_out[0], \n8位加法器_1_p12 , \n8位加法器_1_p13 , \n8位加法器_1_p14 , \n8位加法器_1_p15 , \结果 [7], \结果 [6], \n8位加法器_1_p18 , \结果 [5], \结果 [4], \n8位加法器_1_p21 , \结果 [3], \结果 [2], \结果 [1], \结果 [0], in_12
  \带清零的边缘触发8位锁存器  \u_带清零的边缘触发8位锁存器_1  (
    .\清零 (in_13), .in_10(clock_1_out), .in_1(\n8位加法器_1_p7 ), .in_2(\n8位加法器_1_p10 ), .in_3(\n8位加法器_1_p12 ),
    .in_4(\n8位加法器_1_p13 ), .in_5(\n8位加法器_1_p14 ), .in_6(\n8位加法器_1_p15 ), .in_7(\n8位加法器_1_p18 ),
    .in_8(\n8位加法器_1_p21 ), .out_13(\结果 [7]), .out_14(\结果 [6]), .out_11(\结果 [5]), .out_15(\结果 [4]),
    .out_16(\结果 [3]), .out_17(\结果 [2]), .out_12(\结果 [1]), .out_18(\结果 [0]));

  // Notes on the sheet:
  //   自动加法器
  //   计数器
  //   RAM
  //   控制开关
endmodule

module two (
  input  C0,
  input  in_2,
  input  in_3,
  input  in_4,
  input  in_5,
  output [7:0] out_6
);

  wire clock_1_out, undriven;
  wire [7:0] multiplexer_1_out, \n8位加法器_1_out_26 , ram_2_data, \取反器_1_out_17 , \带清零的边缘触发8位锁存器_1_out_18 ;
  wire [15:0] counter_1_q;

  Clock clock_1 (.out(clock_1_out));
  Counter #(.width(16), .max('hffff)) counter_1 (
    .Q(counter_1_q), .clk(clock_1_out), .clr(in_2));  // open: load, D, count, carry
  RAM #(.addrWidth(16)) ram_1 (.addr(counter_1_q), .data(out_6));  // open: sel, clk, ld, clr
  RAM #(.addrWidth(16), .bus("separate")) ram_2 (
    .addr(counter_1_q), .din(\带清零的边缘触发8位锁存器_1_out_18 ), .data(ram_2_data), .str(undriven));  // open: sel, clk, ld, clr
  Multiplexer #(.width(8), .enable("false")) multiplexer_1 (
    .in0(ram_2_data), .in1(\n8位加法器_1_out_26 ), .out(multiplexer_1_out), .sel(in_3));
  \取反器  \u_取反器_1  (
    .out_10(\取反器_1_out_17 [7]), .out_11(\取反器_1_out_17 [6]), .out_12(\取反器_1_out_17 [5]),
    .out_13(\取反器_1_out_17 [4]), .out_14(\取反器_1_out_17 [3]), .out_15(\取反器_1_out_17 [2]),
    .out_16(\取反器_1_out_17 [1]), .out_17(\取反器_1_out_17 [0]), .in_1(ram_2_data[7]), .in_2(ram_2_data[6]),
    .in_3(ram_2_data[5]), .in_4(ram_2_data[4]), .in_5(ram_2_data[3]), .in_6(ram_2_data[2]),
    .in_7(ram_2_data[1]), .in_8(ram_2_data[0]), .in_9(C0));
  \_8位加法器  \u_8位加法器_1  (
    .in_15(\取反器_1_out_17 [7]), .in_16(\带清零的边缘触发8位锁存器_1_out_18 [7]), .in_5(\取反器_1_out_17 [6]),
    .in_6(\带清零的边缘触发8位锁存器_1_out_18 [6]), .in_7(\取反器_1_out_17 [5]), .in_8(\带清零的边缘触发8位锁存器_1_out_18 [5]),
    .in_9(\取反器_1_out_17 [4]), .in_10(\带清零的边缘触发8位锁存器_1_out_18 [4]), .in_1(\取反器_1_out_17 [3]),
    .in_11(\带清零的边缘触发8位锁存器_1_out_18 [3]), .in_12(\取反器_1_out_17 [2]), .in_13(\带清零的边缘触发8位锁存器_1_out_18 [2]),
    .in_17(\取反器_1_out_17 [1]), .in_14(\带清零的边缘触发8位锁存器_1_out_18 [1]), .in_2(\取反器_1_out_17 [0]),
    .in_3(\带清零的边缘触发8位锁存器_1_out_18 [0]), .in_4(C0), .out_20(\n8位加法器_1_out_26 [7]),
    .out_21(\n8位加法器_1_out_26 [6]), .out_18(\n8位加法器_1_out_26 [5]), .out_19(\n8位加法器_1_out_26 [4]),
    .out_22(\n8位加法器_1_out_26 [3]), .out_23(\n8位加法器_1_out_26 [2]), .out_25(\n8位加法器_1_out_26 [1]),
    .out_26(\n8位加法器_1_out_26 [0]));  // open: out_24
  \带清零的边缘触发8位锁存器  \u_带清零的边缘触发8位锁存器_1  (
    .\清零 (in_4), .in_10(in_5), .in_1(multiplexer_1_out[7]), .in_2(multiplexer_1_out[6]),
    .in_3(multiplexer_1_out[5]), .in_4(multiplexer_1_out[4]), .in_5(multiplexer_1_out[3]),
    .in_6(multiplexer_1_out[2]), .in_7(multiplexer_1_out[1]), .in_8(multiplexer_1_out[0]),
    .out_13(\带清零的边缘触发8位锁存器_1_out_18 [7]), .out_14(\带清零的边缘触发8位锁存器_1_out_18 [6]),
    .out_11(\带清零的边缘触发8位锁存器_1_out_18 [5]), .out_15(\带清零的边缘触发8位锁存器_1_out_18 [4]),
    .out_16(\带清零的边缘触发8位锁存器_1_out_18 [3]), .out_17(\带清零的边缘触发8位锁存器_1_out_18 [2]),
    .out_12(\带清零的边缘触发8位锁存器_1_out_18 [1]), .out_18(\带清零的边缘触发8位锁存器_1_out_18 [0]));

  // Notes on the sheet:
  //   计数器
  //   RAM
  //   W
endmodule

module three (
  input  _13,
  input  clk,
  input  C0,
  input  _12,
  input  _1,
  input  _2,
  input  clk_2,
  input  \零标志 ,
  input  _4,
  input  _3,
  input  _10,
  input  _5,
  input  _6,
  input  _14,
  input  clk_3,
  input  _15,
  input  _17,
  output \进位标志 ,
  output out_19,
  output [7:0] out_20
);

  wire clock_1_out, \n8位加法器_1_out_24 , nor_1_out, not_1_out;
  wire [7:0] multiplexer_2_out, \n8位加法器_1_out_26 , ram_1_data, \取反器_1_out_17 , \边缘触发8位锁存器_1_out_17 ;
  wire [15:0] counter_1_q, multiplexer_1_out, \边缘触发8位锁存器_2_out_17 ;

  Clock clock_1 (.out(clock_1_out));
  Counter #(.width(16), .max('hffff)) counter_1 (
    .load(_2), .D(\边缘触发8位锁存器_2_out_17 ), .count(_1), .Q(counter_1_q), .clk(clock_1_out), .clr(_3));  // open: carry
  Multiplexer #(.width(16), .enable("false")) multiplexer_1 (
    .in0(counter_1_q), .out(multiplexer_1_out), .sel(_4));  // open: in1
  not not_1 (not_1_out, _5);
  RAM #(.addrWidth(16), .bus("separate")) ram_1 (
    .addr(multiplexer_1_out), .din(out_20), .data(ram_1_data), .str(_5), .clk(_6), .ld(not_1_out));  // open: sel, clr
  \边缘触发8位锁存器  \u_边缘触发8位锁存器_1  (
    .in_9(clk), .in_1(ram_1_data[7]), .in_2(ram_1_data[6]), .in_3(ram_1_data[5]), .in_4(ram_1_data[4]),
    .in_5(ram_1_data[3]), .in_6(ram_1_data[2]), .in_7(ram_1_data[1]), .in_8(ram_1_data[0]),
    .out_12(\边缘触发8位锁存器_1_out_17 [7]), .out_13(\边缘触发8位锁存器_1_out_17 [6]), .out_10(\边缘触发8位锁存器_1_out_17 [5]),
    .out_14(\边缘触发8位锁存器_1_out_17 [4]), .out_15(\边缘触发8位锁存器_1_out_17 [3]), .out_16(\边缘触发8位锁存器_1_out_17 [2]),
    .out_11(\边缘触发8位锁存器_1_out_17 [1]), .out_17(\边缘触发8位锁存器_1_out_17 [0]));
  \边缘触发8位锁存器  \u_边缘触发8位锁存器_2  (
    .in_9(clk_2), .in_1(ram_1_data[7]), .in_2(ram_1_data[6]), .in_3(ram_1_data[5]), .in_4(ram_1_data[4]),
    .in_5(ram_1_data[3]), .in_6(ram_1_data[2]), .in_7(ram_1_data[1]), .in_8(ram_1_data[0]),
    .out_12(\边缘触发8位锁存器_2_out_17 [7]), .out_13(\边缘触发8位锁存器_2_out_17 [6]), .out_10(\边缘触发8位锁存器_2_out_17 [5]),
    .out_14(\边缘触发8位锁存器_2_out_17 [4]), .out_15(\边缘触发8位锁存器_2_out_17 [3]), .out_16(\边缘触发8位锁存器_2_out_17 [2]),
    .out_11(\边缘触发8位锁存器_2_out_17 [1]), .out_17(\边缘触发8位锁存器_2_out_17 [0]));
  \边缘触发8位锁存器  \u_边缘触发8位锁存器_3  (
    .in_9(clk_3), .in_1(ram_1_data[7]), .in_2(ram_1_data[6]), .in_3(ram_1_data[5]), .in_4(ram_1_data[4]),
    .in_5(ram_1_data[3]), .in_6(ram_1_data[2]), .in_7(ram_1_data[1]), .in_8(ram_1_data[0]),
    .out_12(\边缘触发8位锁存器_2_out_17 [15]), .out_13(\边缘触发8位锁存器_2_out_17 [14]), .out_10(\边缘触发8位锁存器_2_out_17 [13]),
    .out_14(\边缘触发8位锁存器_2_out_17 [12]), .out_15(\边缘触发8位锁存器_2_out_17 [11]), .out_16(\边缘触发8位锁存器_2_out_17 [10]),
    .out_11(\边缘触发8位锁存器_2_out_17 [9]), .out_17(\边缘触发8位锁存器_2_out_17 [8]));
  \带清零的边缘触发1位锁存器  \u_带清零的边缘触发1位锁存器_1  (.\清零 (_10), .\数据输入 (nor_1_out), .\写操作端 (\零标志 ), .\数据输出 (out_19));
  \带清零的边缘触发1位锁存器  \u_带清零的边缘触发1位锁存器_2  (.\清零 (_12), .\数据输入 (\n8位加法器_1_out_24 ), .\写操作端 (_13), .\数据输出 (\进位标志 ));
  nor nor_1 (nor_1_out, \n8位加法器_1_out_26 [0], \n8位加法器_1_out_26 [1], \n8位加法器_1_out_26 [2], \n8位加法器_1_out_26 [3], \n8位加法器_1_out_26 [4], \n8位加法器_1_out_26 [5], \n8位加法器_1_out_26 [6], \n8位加法器_1_out_26 [7]);
  Multiplexer #(.width(8), .enable("false")) multiplexer_2 (
    .in0(ram_1_data), .in1(\n8位加法器_1_out_26 ), .out(multiplexer_2_out), .sel(_14));
  \取反器  \u_取反器_1  (
    .out_10(\取反器_1_out_17 [7]), .out_11(\取反器_1_out_17 [6]), .out_12(\取反器_1_out_17 [5]),
    .out_13(\取反器_1_out_17 [4]), .out_14(\取反器_1_out_17 [3]), .out_15(\取反器_1_out_17 [2]),
    .out_16(\取反器_1_out_17 [1]), .out_17(\取反器_1_out_17 [0]), .in_1(ram_1_data[7]), .in_2(ram_1_data[6]),
    .in_3(ram_1_data[5]), .in_4(ram_1_data[4]), .in_5(ram_1_data[3]), .in_6(ram_1_data[2]),
    .in_7(ram_1_data[1]), .in_8(ram_1_data[0]), .in_9(C0));
  \_8位加法器  \u_8位加法器_1  (
    .in_15(\取反器_1_out_17 [7]), .in_16(out_20[7]), .in_5(\取反器_1_out_17 [6]), .in_6(out_20[6]),
    .in_7(\取反器_1_out_17 [5]), .in_8(out_20[5]), .in_9(\取反器_1_out_17 [4]), .in_10(out_20[4]),
    .in_1(\取反器_1_out_17 [3]), .in_11(out_20[3]), .in_12(\取反器_1_out_17 [2]), .in_13(out_20[2]),
    .in_17(\取反器_1_out_17 [1]), .in_14(out_20[1]), .in_2(\取反器_1_out_17 [0]), .in_3(out_20[0]), .in_4(C0),
    .out_24(\n8位加法器_1_out_24 ), .out_20(\n8位加法器_1_out_26 [7]), .out_21(\n8位加法器_1_out_26 [6]),
    .out_18(\n8位加法器_1_out_26 [5]), .out_19(\n8位加法器_1_out_26 [4]), .out_22(\n8位加法器_1_out_26 [3]),
    .out_23(\n8位加法器_1_out_26 [2]), .out_25(\n8位加法器_1_out_26 [1]), .out_26(\n8位加法器_1_out_26 [0]));
  \带清零的边缘触发8位锁存器  \u_带清零的边缘触发8位锁存器_1  (
    .\清零 (_15), .in_10(_17), .in_1(multiplexer_2_out[7]), .in_2(multiplexer_2_out[6]),
    .in_3(multiplexer_2_out[5]), .in_4(multiplexer_2_out[4]), .in_5(multiplexer_2_out[3]),
    .in_6(multiplexer_2_out[2]), .in_7(multiplexer_2_out[1]), .in_8(multiplexer_2_out[0]),
    .out_13(out_20[7]), .out_14(out_20[6]), .out_11(out_20[5]), .out_15(out_20[4]), .out_16(out_20[3]),
    .out_17(out_20[2]), .out_12(out_20[1]), .out_18(out_20[0]));

  // Notes on the sheet:
  //   计数器
  //   RAM
  //   W
  //   7
  //   8
  //   9
  //   11
  //   16
endmodule

module \带清零的边缘触发1位锁存器  (
  input  \清零 ,
  input  \数据输入 ,
  input  \写操作端 ,
  output \数据输出 
);

  wire and_1_out, and_2_out, and_3_out, and_4_out, nor_1_out, nor_2_out, nor_4_out, not_1_out, not_2_out;

  not not_1 (not_1_out, \数据输入 );
  not not_2 (not_2_out, \写操作端 );
  and and_1 (and_1_out, \数据输入 , not_2_out);
  and and_2 (and_2_out, not_2_out, not_1_out);
  nor nor_1 (nor_1_out, and_1_out, nor_2_out);
  nor nor_2 (nor_2_out, nor_1_out, and_2_out);
  and and_3 (and_3_out, nor_1_out, \写操作端 );
  and and_4 (and_4_out, \写操作端 , nor_2_out);
  nor nor_3 (\数据输出 , \清零 , and_3_out, nor_4_out);
  nor nor_4 (nor_4_out, \数据输出 , and_4_out);
endmodule
